// Logisim project HITCH8.circ as structural Verilog: 12 circuits, main circuit main
module main (
  input  write_to_BUS,
  input  [7:0] BUS
);

  wire alu_8_bit_1_c_out, alu_8_bit_1_is_zero, alu_8_bit_1_overflow, and_1_out, and_2_out, and_3_out,
       and_4_out, and_5_out, and_6_out, and_7_out, and_8_out, and_9_out, CIN, CLOCK_out, inv_CLOCK, LR, MDI,
       MDO, or_1_out, or_2_out, RAC, ROM, RPC, RR, RSP, RW, SPC, SR, SSP, WA, WAC, WB, WML, WMM, WPC, WSP;
  wire [1:0] SAC;
  wire [2:0] n4_bit_status_reg_1_c_out_2;
  wire [3:0] OS, reg_sel;
  wire [7:0] alu_8_bit_1_r, controlled_buffer_1_out, controlled_buffer_6_out,
       general_purpose_registers_1_out_5, MAR_lsb_q, MAR_msb_q, MDR_q, ram_1_outdata, regA_q, regB_q;
  wire [15:0] program_counter_16_bit_1_data_out_rom, program_counter_16_bit_1_pc_content;
  wire [25:0] eeprom_1_instruction;

  and and_1 (and_1_out, inv_CLOCK, WA);
  and and_2 (and_2_out, inv_CLOCK, WB);
  and and_3 (and_3_out, inv_CLOCK, WML);
  Register_8_bit MAR_msb (.D(controlled_buffer_1_out), .READ_from_bus(and_4_out), .WRITE_to_bus(1'b1), .Q(MAR_msb_q));
  and and_4 (and_4_out, inv_CLOCK, WMM);
  Register_8_bit regA (.D(controlled_buffer_1_out), .READ_from_bus(and_1_out), .WRITE_to_bus(1'b1), .Q(regA_q));
  Register_8_bit regB (.D(controlled_buffer_1_out), .READ_from_bus(and_2_out), .WRITE_to_bus(1'b1), .Q(regB_q));
  ALU_8_bit alu_8_bit_1 (
    .c_in(CIN), .A(regA_q), .B(regB_q), .Selector(OS), .c_out(alu_8_bit_1_c_out), .R(alu_8_bit_1_r),
    .is_zero(alu_8_bit_1_is_zero), .overflow(alu_8_bit_1_overflow));
  RAM ram_1 (.addrMSB(MAR_msb_q), .addrLSB(MAR_lsb_q), .inDATA(MDR_q), .LOAD(LR), .STORE(SR), .outDATA(ram_1_outdata));
  Register_8_bit MAR_lsb (.D(controlled_buffer_1_out), .READ_from_bus(and_3_out), .WRITE_to_bus(1'b1), .Q(MAR_lsb_q));
  _4_bit_status_reg u_4_bit_status_reg_1 (
    .SET(and_5_out), .c_out_2(n4_bit_status_reg_1_c_out_2[0]), .c_out(alu_8_bit_1_c_out),
    .zero(alu_8_bit_1_is_zero), .overflow(alu_8_bit_1_overflow), .zero_2(n4_bit_status_reg_1_c_out_2[1]),
    .overflow_2(n4_bit_status_reg_1_c_out_2[2]));
  assign controlled_buffer_1_out = WAC ? alu_8_bit_1_r : 8'bz;  // Controlled_Buffer controlled_buffer_1
  and and_5 (and_5_out, inv_CLOCK, WAC);
  or or_1 (or_1_out, MDI, LR);
  or or_2 (or_2_out, MDO, SR);
  Accumulator_Register accumulator_register_1 (
    .Data_In(controlled_buffer_1_out), .write_en(and_5_out), .reg_sel(SAC), .read_en(RAC),
    .Data_Out(controlled_buffer_1_out));
  and and_6 (and_6_out, inv_CLOCK, or_1_out);
  Register_8_bit MDR (.D(ram_1_outdata), .READ_from_bus(and_6_out), .WRITE_to_bus(or_2_out), .Q(MDR_q));
  assign controlled_buffer_1_out = MDO ? MDR_q : 8'bz;  // Controlled_Buffer controlled_buffer_2
  assign ram_1_outdata = MDI ? controlled_buffer_1_out : 8'bz;  // Controlled_Buffer controlled_buffer_3
  not not_1 (inv_CLOCK, CLOCK_out);
  and and_7 (and_7_out, inv_CLOCK, WSP);
  Clock CLOCK (.out(CLOCK_out));
  Stack_Pointer_16_bit stack_pointer_16_bit_1 (
    .Data_In(controlled_buffer_1_out), .write_en(and_7_out), .reg_sel(SSP), .read_en(RSP),
    .Data_Out(controlled_buffer_1_out));
  Control_Unit control_unit_1 (
    .INSTRUCTION(eeprom_1_instruction), .status_flags(n4_bit_status_reg_1_c_out_2), .CLOCK(CLOCK_out),
    .write_A(WA), .write_B(WB), .operation_sel(OS), .c_in(CIN), .write_Acc(WAC), .read_Acc(RAC),
    .sel_Acc(SAC), .write_PC(WPC), .read_PC(RPC), .sel_PC(SPC), .read_ROM(ROM), .wr_MAR_L(WML),
    .wr_MAR_M(WMM), .load_from_RAM(LR), .store_to_RAM(SR), .MDR_in(MDI), .MDR_out(MDO), .write_SP(WSP),
    .read_SP(RSP), .sel_SP(SSP), .reg_read(RR), .reg_write(RW), .reg_sel(reg_sel),
    .BUS_out(controlled_buffer_1_out));
  and and_8 (and_8_out, inv_CLOCK, WPC);
  Program_Counter_16_bit program_counter_16_bit_1 (
    .Data_In(controlled_buffer_1_out), .write_en(and_8_out), .reg_sel(SPC), .read_en(RPC),
    .Data_Out(controlled_buffer_1_out), .to_ROM(ROM), .Data_Out_ROM(program_counter_16_bit_1_data_out_rom),
    .PC_content(program_counter_16_bit_1_pc_content));
  // Probe on controlled_buffer_1_out
  assign controlled_buffer_1_out = write_to_BUS ? BUS : 8'bz;  // Controlled_Buffer controlled_buffer_4
  General_Purpose_Registers general_purpose_registers_1 (
    .write(and_9_out), .in_2(controlled_buffer_6_out), .Rsel(reg_sel), .read(RR),
    .out_5(general_purpose_registers_1_out_5));
  and and_9 (and_9_out, inv_CLOCK, RW);
  // Probe on program_counter_16_bit_1_pc_content
  EEPROM eeprom_1 (.address(program_counter_16_bit_1_data_out_rom), .READ(ROM), .instruction(eeprom_1_instruction));
  assign controlled_buffer_1_out = RR ? general_purpose_registers_1_out_5 : 8'bz;  // Controlled_Buffer controlled_buffer_5
  assign controlled_buffer_6_out = RW ? controlled_buffer_1_out : 8'bz;  // Controlled_Buffer controlled_buffer_6

  // Notes on the sheet:
  //    BUS 
  //   4 x 16 bit; 2 x 32 bit. 
  //    BUS 
endmodule

module ALU_8_bit (
  input  c_in,
  input  [7:0] A,
  input  [7:0] B,
  input  [3:0] Selector,
  output c_out,
  output [7:0] R,
  output is_zero,
  output overflow
);

  wire adder_1_cout, and_2_out, and_3_out, B7, multiplexer_6_out, not_3_out, not_4_out, not_5_out, or_2_out;
  wire [6:0] multiplexer_1_out;
  wire [7:0] adder_1_out, and_1_out, bit_extender_1_out, bit_extender_2_out, multiplexer_2_out,
       multiplexer_3_out, multiplexer_4_out, not_1_out, not_2_out, or_1_out, shifter_1_out, shifter_2_out,
       shifter_3_out, xor_1_out;

  assign not_1_out = ~B;  // NOT_Gate not_1, 8 bits wide
  assign bit_extender_1_out = {{7{1'b0}}, 1'b0};  // Bit_Extender bit_extender_1
  assign bit_extender_2_out = {{7{1'b1}}, 1'b1};  // Bit_Extender bit_extender_2
  assign not_2_out = ~A;  // NOT_Gate not_2, 8 bits wide
  assign and_1_out = A & B;  // AND_Gate and_1, 8 bits wide
  assign or_1_out = A | B;  // OR_Gate or_1, 8 bits wide
  assign xor_1_out = A ^ B;  // XOR_Gate xor_1, 8 bits wide
  Multiplexer #(.select(2), .width(8), .enable("false")) multiplexer_1 (
    .in0(B), .in1(not_1_out), .in2(bit_extender_1_out), .in3(bit_extender_2_out),
    .out({B7, multiplexer_1_out}), .sel(Selector[1:0]));
  Shifter #(.shift("lr")) shifter_1 (.in(A), .\dist (3'b001), .out(shifter_1_out));
  Shifter #(.shift("ar")) shifter_2 (.in(A), .\dist (3'b001), .out(shifter_2_out));
  Shifter shifter_3 (.in(A), .\dist (3'b001), .out(shifter_3_out));
  Adder adder_1 (.a(A), .b({B7, multiplexer_1_out}), .out(adder_1_out), .cin(c_in), .cout(adder_1_cout));
  Multiplexer #(.select(2), .width(8), .enable("false")) multiplexer_2 (
    .in0(not_2_out), .in1(and_1_out), .in2(or_1_out), .in3(xor_1_out), .out(multiplexer_2_out),
    .sel(Selector[1:0]));
  Multiplexer #(.width(8), .enable("false")) multiplexer_3 (
    .in0(adder_1_out), .in1(multiplexer_2_out), .out(multiplexer_3_out), .sel(Selector[2]));
  Multiplexer #(.select(2), .width(8), .enable("false")) multiplexer_4 (
    .in0({c_in, shifter_1_out[6:0]}), .in1(shifter_2_out), .in2({shifter_3_out[7:1], c_in}),
    .in3(bit_extender_1_out), .out(multiplexer_4_out), .sel(Selector[1:0]));
  Multiplexer #(.width(8), .enable("false")) multiplexer_5 (
    .in0(multiplexer_3_out), .in1(multiplexer_4_out), .out(R), .sel(Selector[3]));
  Multiplexer #(.select(2), .enable("false")) multiplexer_6 (
    .in0(A[0]), .in1(A[0]), .in2(A[7]), .in3(1'b0), .out(multiplexer_6_out), .sel(Selector[1:0]));
  Multiplexer #(.enable("false")) multiplexer_7 (
    .in0(adder_1_cout), .in1(multiplexer_6_out), .out(c_out), .sel(Selector[3]));
  not not_3 (not_3_out, R[7]);
  not not_4 (not_4_out, A[7]);
  not not_5 (not_5_out, B7);
  or or_2 (or_2_out, R[0], R[1], R[2], R[3], R[4], R[5], R[6], R[7]);
  and and_2 (and_2_out, not_3_out, B7, A[7]);
  and and_3 (and_3_out, R[7], not_4_out, not_5_out);
  not not_6 (is_zero, or_2_out);
  or or_3 (overflow, and_2_out, and_3_out);

  // Other names for the same wires on the sheet: cin = c_in; sel_1_0[1:0] = Selector[1:0]; sel_2 = Selector[2];
  //   sel_3 = Selector[3]

  // Notes on the sheet:
  //   0000 -> A+B+c_in
  //   0100 -> not(A)
  //   0101 -> A and B
  //   0110 -> A or B
  //   0111 -> A xor B
  //   1000 -> A>>1 logico
  //   1001 -> A>>1 aritmetico
  //   1010 -> A<<1
  //   0001 -> A-B (A+ not(B) + c_in)
  //   0010 -> A+c_in (increment if c_in=1)
  //   0011 -> A-1+c_in (decrement if c_in=0)
  //   8-bit AND
  //   8-bit OR
  //   8-bit XOR
  //   00 -> B
  //   01 -> -B
  //   10 -> 0
  //   11 -> -1
  //   8-bit adder
  //   IN CASE OF SHIFT OPERATIONS:
  //   c_out = bit that goes out
  //   c_in = bit that goes in, if any
  //   00 -> not(A)
  //   01 -> AandB
  //   10 -> AorB
  //   11 -> -AxorB
  //   00 -> A>>1 (logic shift)
  //   01 -> A>>1 (aritm shift)
  //   10 -> A<<1 (logic shift)
  //   00 -> A>>1 (logic shift) -> pass bit 0
  //   01 -> A>>1 (aritm shift) -> pass bit 0
  //   10 -> A<<1 (logic shift) -> pass bit 7
endmodule

module _4_bit_status_reg (
  input  c_out,
  input  zero,
  input  overflow,
  input  SET,
  output c_out_2,
  output zero_2,
  output overflow_2
);

  wire [3:3] register_1_q;

  Register #(.width(4)) register_1 (
    .D({1'b0, overflow, zero, c_out}), .en(SET), .Q({register_1_q[3], overflow_2, zero_2, c_out_2}),
    .clk(SET), .clr(1'b0));
endmodule

module Register_8_bit (
  input  [7:0] D,
  input  READ_from_bus,
  input  WRITE_to_bus,
  output [7:0] Q
);

  wire [7:0] register_1_q;

  Register register_1 (.D(D), .en(READ_from_bus), .Q(register_1_q), .clk(READ_from_bus), .clr(1'b0));
  assign Q = WRITE_to_bus ? register_1_q : 8'bz;  // Controlled_Buffer controlled_buffer_1
endmodule

module Register_4_bit (
  input  [3:0] D,
  input  READ_from_bus,
  input  WRITE_to_bus,
  output [3:0] Q
);

  wire [3:0] register_1_q;

  Register #(.width(4)) register_1 (.D(D), .en(READ_from_bus), .Q(register_1_q), .clk(READ_from_bus), .clr(1'b0));
  assign Q = WRITE_to_bus ? register_1_q : 4'bz;  // Controlled_Buffer controlled_buffer_1
endmodule

module RAM (
  input  [7:0] addrMSB,
  input  [7:0] addrLSB,
  input  [7:0] inDATA,
  input  LOAD,
  input  STORE,
  output [7:0] outDATA
);

  wire or_1_out;
  wire [7:0] ram_1_data;

  or or_1 (or_1_out, LOAD, STORE);
  RAM_part #(.addrWidth(16), .bus("asynch")) ram_1 (
    .addr({addrMSB, addrLSB}), .data(ram_1_data), .sel(or_1_out), .ld(LOAD), .clr(1'b0));
  assign outDATA = LOAD ? ram_1_data : 8'bz;  // Controlled_Buffer controlled_buffer_1
  assign ram_1_data = STORE ? inDATA : 8'bz;  // Controlled_Buffer controlled_buffer_2
endmodule

module General_Purpose_Registers (
  input  write,
  input  [7:0] in_2,
  input  [3:0] Rsel,
  input  read,
  output [7:0] out_5
);

  wire _0l, _0m, _1l, _1m, _2l, _2m, _3l, _3m, _4lh, _4ll, _4mh, _4ml, _5lh, _5ll, _5mh, _5ml, and_1_out,
       and_2_out, and_3_out, and_4_out, and_5_out, and_6_out, and_7_out, and_8_out, and_9_out, and_10_out,
       and_11_out, and_12_out, and_13_out, and_14_out, and_15_out, and_16_out, and_17_out, and_18_out,
       and_19_out, and_20_out, and_21_out, and_22_out, and_23_out, and_24_out, and_25_out, and_26_out,
       and_27_out, and_28_out, and_29_out, and_30_out, and_31_out, and_32_out;
  wire [7:0] R0m_q;

  Decoder #(.select(4), .disabled(0), .enable("false")) decoder_1 (
    .out0(_0l), .out1(_0m), .out2(_1l), .out3(_1m), .out4(_2l), .out5(_2m), .out6(_3l), .out7(_3m),
    .out8(_4ll), .out9(_4lh), .out10(_4ml), .out11(_4mh), .out12(_5ll), .out13(_5lh), .out14(_5ml),
    .out15(_5mh), .sel(Rsel));
  and and_1 (and_1_out, write, _0m);
  and and_2 (and_2_out, _5mh, read);
  and and_3 (and_3_out, write, _1m);
  and and_4 (and_4_out, _4mh, read);
  and and_5 (and_5_out, write, _2m);
  and and_6 (and_6_out, _3m, read);
  and and_7 (and_7_out, write, _3m);
  and and_8 (and_8_out, _2m, read);
  and and_9 (and_9_out, write, _4mh);
  and and_10 (and_10_out, _1m, read);
  and and_11 (and_11_out, write, _5mh);
  and and_12 (and_12_out, _0m, read);
  Register_8_bit R0m (.D(R0m_q), .READ_from_bus(and_1_out), .WRITE_to_bus(and_12_out), .Q(R0m_q));
  Register_8_bit R1m (.D(R0m_q), .READ_from_bus(and_3_out), .WRITE_to_bus(and_10_out), .Q(R0m_q));
  Register_8_bit R2m (.D(R0m_q), .READ_from_bus(and_5_out), .WRITE_to_bus(and_8_out), .Q(R0m_q));
  Register_8_bit R3m (.D(R0m_q), .READ_from_bus(and_7_out), .WRITE_to_bus(and_6_out), .Q(R0m_q));
  Register_8_bit R4mh (.D(R0m_q), .READ_from_bus(and_9_out), .WRITE_to_bus(and_4_out), .Q(R0m_q));
  Register_8_bit R5mh (.D(R0m_q), .READ_from_bus(and_11_out), .WRITE_to_bus(and_2_out), .Q(R0m_q));
  and and_13 (and_13_out, _5ml, write);
  Register_8_bit R0l (.D(R0m_q), .READ_from_bus(and_29_out), .WRITE_to_bus(and_32_out), .Q(R0m_q));
  Register_8_bit R1l (.D(R0m_q), .READ_from_bus(and_25_out), .WRITE_to_bus(and_28_out), .Q(R0m_q));
  Register_8_bit R2l (.D(R0m_q), .READ_from_bus(and_21_out), .WRITE_to_bus(and_24_out), .Q(R0m_q));
  Register_8_bit R3l (.D(R0m_q), .READ_from_bus(and_17_out), .WRITE_to_bus(and_20_out), .Q(R0m_q));
  Register_8_bit R4ml (.D(R0m_q), .READ_from_bus(and_15_out), .WRITE_to_bus(and_16_out), .Q(R0m_q));
  Register_8_bit R5ml (.D(R0m_q), .READ_from_bus(and_13_out), .WRITE_to_bus(and_14_out), .Q(R0m_q));
  and and_14 (and_14_out, _5ml, read);
  and and_15 (and_15_out, write, _4ml);
  and and_16 (and_16_out, _4ml, read);
  and and_17 (and_17_out, write, _3l);
  and and_18 (and_18_out, write, _4lh);
  Register_8_bit R4lh (.D(R0m_q), .READ_from_bus(and_18_out), .WRITE_to_bus(and_23_out), .Q(R0m_q));
  Register_8_bit R5lh (.D(R0m_q), .READ_from_bus(and_22_out), .WRITE_to_bus(and_19_out), .Q(R0m_q));
  and and_19 (and_19_out, _5lh, read);
  and and_20 (and_20_out, _3l, read);
  and and_21 (and_21_out, write, _2l);
  and and_22 (and_22_out, write, _5lh);
  and and_23 (and_23_out, _4lh, read);
  and and_24 (and_24_out, _2l, read);
  and and_25 (and_25_out, write, _1l);
  assign R0m_q = write ? in_2 : 8'bz;  // Controlled_Buffer controlled_buffer_1
  assign out_5 = read ? R0m_q : 8'bz;  // Controlled_Buffer controlled_buffer_2
  and and_26 (and_26_out, write, _4ll);
  Register_8_bit R4ll (.D(R0m_q), .READ_from_bus(and_26_out), .WRITE_to_bus(and_31_out), .Q(R0m_q));
  Register_8_bit R5ll (.D(R0m_q), .READ_from_bus(and_30_out), .WRITE_to_bus(and_27_out), .Q(R0m_q));
  and and_27 (and_27_out, _5ll, read);
  and and_28 (and_28_out, _1l, read);
  and and_29 (and_29_out, write, _0l);
  and and_30 (and_30_out, write, _5ll);
  and and_31 (and_31_out, _4ll, read);
  and and_32 (and_32_out, _0l, read);
endmodule

module EEPROM (
  input  [15:0] address,
  input  READ,
  output [25:0] instruction
);

  wire [25:0] rom_1_data;

  ROM #(.addrWidth(13), .dataWidth(26)) rom_1 (.addr(address[12:0]), .data(rom_1_data), .sel(1'b1));
  assign instruction = READ ? rom_1_data : 26'bz;  // Controlled_Buffer controlled_buffer_1

  // Notes on the sheet:
  //   contents of rom_1 (hex, n*v repeats v):
  //   0 3400000 2f00100 3410000 2f00100 3640000 2f00200 3680000 2f0fc00 36a0000 2f00200 3000200 35e0000
  //   300fc00 35c0000 3000200 3560000 3000100 3330000 3000100 3320000 37003e8 978*0 100000
endmodule

module Accumulator_Register (
  input  [7:0] Data_In,
  input  write_en,
  input  [1:0] reg_sel,
  input  read_en,
  output [7:0] Data_Out
);

  wire decoder_1_out0, decoder_1_out1, decoder_1_out2, decoder_1_out3, decoder_2_out0, decoder_2_out1,
       decoder_2_out2, decoder_2_out3;
  wire [7:0] Acc0_q;

  Decoder #(.select(2), .disabled(0)) decoder_1 (
    .out0(decoder_1_out0), .out1(decoder_1_out1), .out2(decoder_1_out2), .out3(decoder_1_out3),
    .sel(reg_sel), .en(write_en));
  Decoder #(.select(2), .disabled(0)) decoder_2 (
    .out0(decoder_2_out0), .out1(decoder_2_out1), .out2(decoder_2_out2), .out3(decoder_2_out3),
    .sel(reg_sel), .en(read_en));
  Register_8_bit Acc0 (.D(Data_In), .READ_from_bus(decoder_1_out0), .WRITE_to_bus(decoder_2_out0), .Q(Acc0_q));
  Register_8_bit Acc1 (.D(Data_In), .READ_from_bus(decoder_1_out1), .WRITE_to_bus(decoder_2_out1), .Q(Acc0_q));
  Register_8_bit Acc2 (.D(Data_In), .READ_from_bus(decoder_1_out2), .WRITE_to_bus(decoder_2_out2), .Q(Acc0_q));
  Register_8_bit Acc3 (.D(Data_In), .READ_from_bus(decoder_1_out3), .WRITE_to_bus(decoder_2_out3), .Q(Acc0_q));
  assign Data_Out = read_en ? Acc0_q : 8'bz;  // Controlled_Buffer controlled_buffer_1
endmodule

module Stack_Pointer_16_bit (
  input  [7:0] Data_In,
  input  write_en,
  input  reg_sel,
  input  read_en,
  output [7:0] Data_Out
);

  wire decoder_1_out0, decoder_1_out1, decoder_2_out0, decoder_2_out1;
  wire [7:0] Acc0_q;

  Decoder #(.disabled(0)) decoder_1 (.out0(decoder_1_out0), .out1(decoder_1_out1), .sel(reg_sel), .en(write_en));
  Decoder #(.disabled(0)) decoder_2 (.out0(decoder_2_out0), .out1(decoder_2_out1), .sel(reg_sel), .en(read_en));
  Register_8_bit Acc0 (.D(Data_In), .READ_from_bus(decoder_1_out0), .WRITE_to_bus(decoder_2_out0), .Q(Acc0_q));
  Register_8_bit Acc1 (.D(Data_In), .READ_from_bus(decoder_1_out1), .WRITE_to_bus(decoder_2_out1), .Q(Acc0_q));
  assign Data_Out = read_en ? Acc0_q : 8'bz;  // Controlled_Buffer controlled_buffer_1
endmodule

module Program_Counter_16_bit (
  input  [7:0] Data_In,
  input  write_en,
  input  reg_sel,
  input  read_en,
  input  to_ROM,
  output [15:0] PC_content,
  output [7:0] Data_Out,
  output [15:0] Data_Out_ROM
);

  wire and_1_out, and_2_out, decoder_1_out0, decoder_1_out1, not_1_out;

  Decoder #(.disabled(0)) decoder_1 (.out0(decoder_1_out0), .out1(decoder_1_out1), .sel(reg_sel), .en(write_en));
  Register_8_bit Acc0 (.D(Data_In), .READ_from_bus(decoder_1_out0), .WRITE_to_bus(1'b1), .Q(PC_content[7:0]));
  Register_8_bit Acc1 (.D(Data_In), .READ_from_bus(decoder_1_out1), .WRITE_to_bus(1'b1), .Q(PC_content[15:8]));
  assign Data_Out_ROM = to_ROM ? PC_content : 16'bz;  // Controlled_Buffer controlled_buffer_1
  not not_1 (not_1_out, reg_sel);
  and and_1 (and_1_out, not_1_out, read_en);
  and and_2 (and_2_out, read_en, reg_sel);
  assign Data_Out = and_1_out ? PC_content[7:0] : 8'bz;  // Controlled_Buffer controlled_buffer_2
  assign Data_Out = and_2_out ? PC_content[15:8] : 8'bz;  // Controlled_Buffer controlled_buffer_3

  // Notes on the sheet:
  //   not an actual output, just for debug!
endmodule

module Control_Unit (
  input  [25:0] INSTRUCTION,
  input  [2:0] status_flags,
  input  CLOCK,
  output write_A,
  output c_in,
  output read_Acc,
  output read_PC,
  output read_ROM,
  output wr_MAR_M,
  output store_to_RAM,
  output MDR_out,
  output read_SP,
  output reg_read,
  output [3:0] operation_sel,
  output [1:0] sel_Acc,
  output write_B,
  output write_Acc,
  output write_PC,
  output sel_PC,
  output wr_MAR_L,
  output load_from_RAM,
  output MDR_in,
  output write_SP,
  output sel_SP,
  output reg_write,
  output [7:0] BUS_out,
  output [3:0] reg_sel
);

  wire and_1_out, CU_int_4bit, CU_int_8bit_16bit_msb, CU_int_16bit_lsb, CU_op1_reg, CU_op2_reg, CU_read,
       CU_res_reg, decoder_1_out0, decoder_2_out0, not_1_out, or_1_out;
  wire [1:0] CU_op1_2_res_reg, CU_reg_inc, CU_to_BUS;
  wire [3:0] adder_1_out, controlled_buffer_1_out, int_4bit, result_reg;
  wire [7:0] int_16bit_lsb;
  wire [7:2] _25_24_q;
  wire [7:4] int_8bit;
  wire [9:0] step_counter_q;

  not not_1 (not_1_out, CLOCK);
  and and_1 (and_1_out, CU_read, not_1_out);
  Register_8_bit _25_24 (
    .D({{6{1'b0}}, INSTRUCTION[25:24]}), .READ_from_bus(and_1_out), .WRITE_to_bus(1'b1),
    .Q({_25_24_q, step_counter_q[9:8]}));
  Counter #(.width(4), .max('hf)) step_counter (
    .load(1'b0), .count(1'b1), .Q(step_counter_q[3:0]), .clk(CLOCK), .clr(1'b0));  // open: D, carry
  Register_8_bit _23_16 (
    .D(INSTRUCTION[23:16]), .READ_from_bus(and_1_out), .WRITE_to_bus(1'b1),
    .Q({step_counter_q[7:4], result_reg}));
  // Probe on step_counter_q[3:0]
  Register_8_bit _15_8 (
    .D(INSTRUCTION[15:8]), .READ_from_bus(and_1_out), .WRITE_to_bus(1'b1), .Q({int_8bit, int_4bit}));
  Register_8_bit _7_0 (.D(INSTRUCTION[7:0]), .READ_from_bus(and_1_out), .WRITE_to_bus(1'b1), .Q(int_16bit_lsb));
  nor nor_1 (CU_read, step_counter_q[0], step_counter_q[1], step_counter_q[2], step_counter_q[3]);
  Decoder #(.select(2), .enable("false")) decoder_1 (
    .out0(decoder_1_out0), .out1(CU_res_reg), .out2(CU_op1_reg), .out3(CU_op2_reg), .sel(CU_op1_2_res_reg));
  assign controlled_buffer_1_out = CU_res_reg ? result_reg : 4'bz;  // Controlled_Buffer controlled_buffer_1
  assign controlled_buffer_1_out = CU_op2_reg ? int_4bit : 4'bz;  // Controlled_Buffer controlled_buffer_2
  assign controlled_buffer_1_out = CU_op1_reg ? int_8bit : 4'bz;  // Controlled_Buffer controlled_buffer_3
  Adder #(.width(4)) adder_1 (
    .a(controlled_buffer_1_out), .b({2'b00, CU_reg_inc}), .out(adder_1_out), .cin(1'b0));  // open: cout
  or or_1 (or_1_out, CU_res_reg, CU_op1_reg, CU_op2_reg);
  assign reg_sel = or_1_out ? adder_1_out : 4'bz;  // Controlled_Buffer controlled_buffer_4
  ROM #(.addrWidth(13), .dataWidth(32)) rom_1 (
    .addr({status_flags, step_counter_q}),
    .data({write_A, write_B, operation_sel, c_in, write_Acc, read_Acc, sel_Acc, write_PC, read_PC, sel_PC, read_ROM, wr_MAR_L, wr_MAR_M, load_from_RAM, store_to_RAM, MDR_in, MDR_out, write_SP, read_SP, sel_SP, reg_read, reg_write, CU_op1_2_res_reg, CU_reg_inc, CU_to_BUS}),
    .sel(1'b1));
  Decoder #(.select(2), .enable("false")) decoder_2 (
    .out0(decoder_2_out0), .out1(CU_int_4bit), .out2(CU_int_8bit_16bit_msb), .out3(CU_int_16bit_lsb),
    .sel(CU_to_BUS));
  assign BUS_out = CU_int_16bit_lsb ? int_16bit_lsb : 8'bz;  // Controlled_Buffer controlled_buffer_5
  assign BUS_out = CU_int_8bit_16bit_msb ? {int_8bit, int_4bit} : 8'bz;  // Controlled_Buffer controlled_buffer_6
  assign BUS_out = CU_int_4bit ? {4'b0000, int_4bit} : 8'bz;  // Controlled_Buffer controlled_buffer_7

  // Other names for the same wires on the sheet: EEPROM_1[7:0] = {reg_read, reg_write, CU_op1_2_res_reg, CU_reg_inc, CU_to_BUS};
  //   EEPROM_2[7:0] = {wr_MAR_M, load_from_RAM, store_to_RAM, MDR_in, MDR_out, write_SP, read_SP, sel_SP};
  //   EEPROM_3[7:0] = {read_Acc, sel_Acc, write_PC, read_PC, sel_PC, read_ROM, wr_MAR_L};
  //   EEPROM_4[7:0] = {write_A, write_B, operation_sel, c_in, write_Acc}; int_8bit[3:0] = int_4bit;
  //   int_16bit_msb[7:0] = {int_8bit, int_4bit}; op_2_reg[3:0] = int_4bit; op_1_reg[3:0] = int_8bit

  // Notes on the sheet:
  //   microcode STEP
  //   CONTROL SIGNALS
  //   ...bit 19
  //   read CU only when 0
  //   bit 0...
  //   opCode 6 bit
  //   status flags 3 bit
  //   microcode step 4 bit
  //   microcode ROM
  //   contents of rom_1 (hex, n*v repeats v):
  //   8a0a0000 b100000 880c0000 9340000 12*0 8a0a0000 b100000 880c0000 9340000 8c080000 d100000 8c0c0000
  //   d340000 8*0 8a0a0000 b100000 880c0000 9340000 940000a0 540000b0 15000050 9*0 8a0a0000 b100000
  //   880c0000 9340000 980000a0 580000b0 19000050 9*0 8a0a0000 b100000 880c0000 9340000 940000a0 540000b0
  //   15000050 942000a4 542000b4 15200054 6*0 8a0a0000 b100000 880c0000 9340000 980000a0 580000b0 19000050
  //   982000a4 582000b4 19200054 6*0 8a0a0000 b100000 880c0000 9340000 a80000a0 29000050 10*0 8a0a0000
  //   b100000 880c0000 9340000 a00000a0 21000050 10*0 8a0a0000 b100000 880c0000 9340000 a40000a0 25000050
  //   10*0 8a0a0000 b100000 880c0000 9340000 a80000a0 29000050 a82000a4 29200054 8*0 8a0a0000 b100000
  //   880c0000 9340000 a02000a4 21200054 a00000a0 21000050 8*0 8a0a0000 b100000 880c0000 9340000 a42000a4
  //   25200054 a00000a0 21000050 8*0 8a0a0000 b100000 880c0000 9340000 a80000a0 29000050 a82000a4 29200054
  //   a84000a8 29400058 a86000ac 2960005c 4*0 8a0a0000 b100000 880c0000 9340000 a06000ac 2160005c a04000a8
  //   21400058 a02000a4 21200054 a00000a0 21000050 4*0 8a0a0000 b100000 880c0000 9340000 a46000ac 2560005c
  //   a04000a8 21400058 a02000a4 21200054 a00000a0 21000050 4*0 8a0a0000 b100000 880c0000 9340000 800000a0
  //   400000b0 1000050 802000a4 402000b4 1200054 6*0 8a0a0000 b100000 880c0000 9340000 860000a0 460000b0
  //   7000050 842000a4 442000b4 5200054 6*0 8a0a0000 b100000 880c0000 9340000 800000a0 400000b0 1000050
  //   802000a4 402000b4 1200054 804000a8 404000b8 1400058 806000ac 406000bc 160005c 8a0a0000 b100000
  //   880c0000 9340000 860000a0 460000b0 7000050 842000a4 442000b4 5200054 844000a8 444000b8 5400058
  //   846000ac 446000bc 560005c 8a0a0000 b100000 880c0000 9340000 10003 8001 4000 850 8*0 8a0a0000 b100000
  //   880c0000 9340000 10003 8001 3090 9*0 8a0a0000 b100000 880c0000 9340000 80010003 8001 4000 850
  //   b010000 80000001 0 4000 854 0 0 0 8a0a0000 b100000 880c0000 9340000 80010003 8001 3090 b010000
  //   80000001 0 3094 5*0 8a0a0000 b100000 880c0000 9340000 800000a0 400000b0 1000050 9*0 8a0a0000 b100000
  //   880c0000 9340000 860000a0 460000b0 7000050 9*0 8a0a0000 b100000 880c0000 9340000 88000090 9000000
  //   10*0 8a0a0000 b100000 880c0000 9340000 88000090 9000000 29000000 100003 140002 7*0 8a0a0000 b100000
  //   880c0000 9340000 88000090 9000000 29000000 100003 140002 7*0 8a0a0000 b100000 880c0000 9340000
  //   88000090 9000000 29000000 9*0 8a0a0000 b100000 880c0000 9340000 88000090 9000000 29000000 9*0
  //   8a0a0000 b100000 880c0000 9340000 88000090 9000000 10*0 8a0a0000 b100000 880c0000 9340000 88200094
  //   9200000 0 29200000 100003 140002 6*0 8a0a0000 b100000 880c0000 9340000 88200094 9200000 29200000
  //   100003 140002 7*0 8a0a0000 b100000 880c0000 9340000 88200094 9200000 29200000 9*0 8a0a0000 b100000
  //   880c0000 9340000 88200094 9200000 0 29200000 8*0 8a0a0000 b100000 880c0000 9340000 88000090 9000000
  //   10*0 8a0a0000 b100000 880c0000 9340000 8860009c 9600000 0 29600000 4*0 100003 140002 0 0 8a0a0000
  //   b100000 880c0000 9340000 8860009c 9600000 29600000 100003 140002 7*0 8a0a0000 b100000 880c0000
  //   9340000 8860009c 9600000 29600000 9*0 8a0a0000 b100000 880c0000 9340000 8860009c 9600000 0 29600000
  //   8*0 8a0a0000 b100000 880c0000 9340000 800000a0 9000000 800050 9*0 8a0a0000 b100000 880c0000 9340000
  //   52 11*0 8a0a0000 b100000 880c0000 9340000 800000a0 9000000 800000a4 9200000 800050 a00054 6*0
  //   8a0a0000 b100000 880c0000 9340000 53 56 10*0 8a0a0000 b100000 880c0000 9340000 800000a0 9000000
  //   800000a4 9200000 800000a8 9400000 800000ac 9600000 800050 a00054 c00058 e0005c 8a0a0000 b100000
  //   880c0000 9340000 800000a0 40000003 1000050 9*0 8a0a0000 b100000 880c0000 9340000 860000a0 46000003
  //   7000050 9*0 8a0a0000 b100000 880c0000 9340000 80000200 40000002 1000000 80000300 9200000 800400
  //   a00500 5*0 8a0a0000 b100000 880c0000 9340000 80000200 40000002 7000000 80000300 40000003 5200000
  //   800400 a00500 4*0 8a0a0000 b100000 880c0000 9340000 250 354 10*0 8a0a0000 b100000 880c0000 9340000
  //   403 503 10*0 8a0a0000 b100000 880c0000 9340000 10200 8300 4000 850 8*0 8a0a0000 b100000 880c0000
  //   9340000 10200 8300 3090 9*0 8a0a0000 b100000 880c0000 9340000 80010200 8300 4000 8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
endmodule
